# Fritzing sketch MoistureServoProMini9V (saved by Fritzing 0.9.2b)
circuit board: 3.69603cm x 3.77562cm
breadboards: 1

parts:
  J1 = Basic Servo
  PART1 = SparkFun Soil Moisture Sensor [part_number=SEN-13322]
  part = Battery block 9V
  Part1 = Arduino Pro Mini v13

nets:
  GND: J1.gnd, PART1.GND, part.-, Part1.GND
  VCC: J1.vcc, PART1.VCC, Part1.VCC
  N1: J1.pulse, Part1.D3_PWM
  N2: PART1.SIG, Part1.A0
  N3: part.+, Part1.RAW

custom parts:
  SparkFun Soil Moisture Sensor: The SparkFun Soil Moisture Sensor is a simple breakout for measuring the moisture in soil and similar materials.
